# Fritzing sketch 1_blink (saved by Fritzing 0.8.3b)
breadboards: 1

parts:
  Part1 = Arduino Uno (Rev3)
  LED1 = LED - 5mm [color="Red (633nm)" package="5 mm [THT]"]
  R4 = Resistor [tolerance=±5% resistance=330k package=THT]

nets:
  N1: Part1.ICSP_SCK, Part1.D13/SCK, LED1.anode
  N2: Part1.GND, R4.Pin_1
  N3: LED1.cathode, R4.Pin_0
