# Fritzing sketch 2_3_blink_button (saved by Fritzing 0.8.3b)
breadboards: 1

parts:
  Part1 = Arduino Uno (Rev3)
  LED1 = LED - 5mm [color="Red (633nm)" package="5 mm [THT]"]
  S1 = Pushbutton [package="[THT]"]
  R3 = Resistor [tolerance=±5% resistance=10k package=THT]
  R4 = Resistor [tolerance=±5% resistance=330k package=THT]

nets:
  N1: Part1.ICSP_SCK, Part1.D13/SCK, LED1.anode
  N2: Part1.GND, R3.Pin_1, R4.Pin_1
  N3: Part1.D2, S1.Pin_1, S1.Pin_2, R3.Pin_0
  N4: Part1.5V, S1.Pin_3, S1.Pin_4
  N5: LED1.cathode, R4.Pin_0
