# Fritzing sketch 4_analog_in_pot (saved by Fritzing 0.8.3b)
breadboards: 1

parts:
  Part1 = Arduino Uno (Rev3)
  R5 = Rotary Potentiometer (Small)

nets:
  N1: Part1.A0, R5.wiper
  N2: Part1.GND, R5.leg1
  N3: Part1.5V, R5.leg2
