# Fritzing sketch 5_pot_controlled_led (saved by Fritzing 0.8.3b)
breadboards: 1

parts:
  Part1 = Arduino Uno (Rev3)
  LED1 = LED - 5mm [color="Red (633nm)" package="5 mm [THT]"]
  R2 = Resistor [tolerance=±5% resistance=330k package=THT]
  R5 = Rotary Potentiometer (Small)

nets:
  N1: Part1.A0, R5.wiper
  N2: Part1.GND, R2.Pin_1, R5.leg1
  N3: Part1.D3_PWM, LED1.anode
  N4: Part1.5V, R5.leg2
  N5: LED1.cathode, R2.Pin_0
