# Fritzing sketch 6_rgb_led (saved by Fritzing 0.8.3b)
breadboards: 1

parts:
  Part1 = Arduino Uno (Rev3)
  R4 = Resistor [tolerance=±5% resistance=330k package=THT]
  LED2 = RGB LED (com. anode, rbg) [package="5 mm [THT]"]
  R5 = Resistor [tolerance=±5% resistance=330k package=THT]
  R6 = Resistor [tolerance=±5% resistance=330k package=THT]

nets:
  N1: Part1.ICSP_MOSI, Part1.D11_PWM/MOSI, R4.Pin_1
  N2: Part1.GND, LED2.common_anode
  N3: Part1.D9_PWM, R6.Pin_1
  N4: Part1.D10_PWM/SS, R5.Pin_1
  N5: R4.Pin_0, LED2.red_cathode
  N6: LED2.blue_cathode, R5.Pin_0
  N7: LED2.green_cathode, R6.Pin_0
