# Fritzing sketch 7_night_light (saved by Fritzing 0.8.3b)
breadboards: 1

parts:
  Part1 = Arduino Uno (Rev3)
  LED1 = LED - 5mm [color="Red (633nm)" package="5 mm [THT]"]
  R2 = Resistor [tolerance=±5% resistance=330k package=THT]
  R3 = Resistor [tolerance=±5% resistance=10k package=THT]
  R4 = Photocell (LDR) [package=THT]

nets:
  N1: Part1.A0, R3.Pin_1, R4.pin_0
  N2: Part1.GND, R2.Pin_1, R3.Pin_0
  N3: Part1.D3_PWM, LED1.anode
  N4: Part1.5V, R4.pin_1
  N5: LED1.cathode, R2.Pin_0
