# Fritzing sketch 8_flex_sensor (saved by Fritzing 0.8.3b)
breadboards: 1

parts:
  Part1 = Arduino Uno (Rev3)
  R3 = Resistor [tolerance=±5% resistance=10k package=THT]
  R4 = Basic Force Sensing Resistor (FSR) [package=THT]
  LED1 = LED - 5mm [color="Red (633nm)" package="5 mm [THT]"]
  LED2 = LED - 5mm [color="Yellow (585nm)" package="5 mm [THT]"]
  R5 = Resistor [tolerance=±5% resistance=330k package=THT]
  R6 = Resistor [tolerance=±5% resistance=330k package=THT]

nets:
  N1: Part1.GND, R3.Pin_0, R5.Pin_1, R6.Pin_1
  N2: Part1.D2, LED1.anode
  N3: Part1.D3_PWM, LED2.anode
  N4: Part1.5V, R4.pin_1
  N5: Part1.VIN, R3.Pin_1, R4.pin_0
  N6: LED1.cathode, R5.Pin_0
  N7: LED2.cathode, R6.Pin_0
