# Fritzing sketch 8_with_soft_pot (saved by Fritzing 0.8.3b)
breadboards: 1

parts:
  R1 = Rotary Potentiometer (Small)
  Part1 = Arduino Uno (Rev3)
  R2 = Resistor [tolerance=±5% resistance=10k package=THT]

nets:
  N1: R1.leg1, Part1.GND, R2.Pin_1
  N2: R1.wiper, Part1.A0, R2.Pin_0
  N3: R1.leg2, Part1.5V
