# Fritzing sketch 8_with_thermistor (saved by Fritzing 0.8.3b)
breadboards: 1

parts:
  Part1 = Arduino Uno (Rev3)
  R3 = Resistor [tolerance=±5% resistance=10k package=THT]
  R5 = Temperature Sensor (Thermistor) [thermistor_type=NTC package=THT]

nets:
  N1: Part1.A0, R3.Pin_1, R5.pin_0
  N2: Part1.GND, R3.Pin_0
  N3: Part1.5V, R5.pin_1
